// Logisim project Lab2solution.circ as structural Verilog: 3 circuits, main circuit majority circuit
module majority_circuit (
  input  a,
  input  b,
  input  c,
  output x
);

  wire a_b_out, a_c_out, b_c_out;

  and b_c (b_c_out, b, c);
  and a_c (a_c_out, a, c);
  and a_b (a_b_out, a, b);
  or b_c___a_c___a_b (x, b_c_out, a_c_out, a_b_out);
endmodule

module adder_circuit__9 (
  input  a,
  input  b,
  output sum,
  output carry
);

  wire and_2_out, and_3_out, not_1_out, not_2_out;

  not not_1 (not_1_out, a);
  not not_2 (not_2_out, b);
  and and_1 (carry, a, b);
  and and_2 (and_2_out, not_1_out, b);
  and and_3 (and_3_out, a, not_2_out);
  or or_1 (sum, and_2_out, and_3_out);
endmodule

module adder_circuit__10 (
  input  carryIn,
  input  a,
  input  b,
  output sum,
  output carryOut
);

  wire and_1_out;

  or or_1 (sum, b, a, carryIn);
  and and_1 (and_1_out, a, b);
  or or_2 (carryOut, and_1_out, carryIn);
endmodule
